// Logisim project EP3.circ as structural Verilog: 16 circuits, main circuit main
module main (
  input  [15:0] INPUT,
  output [15:0] OUTPUT
);

  wire and_1_out, and_2_out, and_3_out, and_4_out, and_5_out, and_6_out, and_7_out, clock_1_out,
       \clock_com_meia_frequência_q , \clock_com_meia_frequência_qn , d_ff_1_q, d_ff_2_qn, d_ff_3_qn,
       d_ff_4_qn, \Escreverá_do_endereço_out , eu_sei_que_vai_ser_sempre_1__mas_fica_mais_intuitivo_out,
       \instrucao_0a_1_é_a_instrução_0a , \instrucao_0f_1_é_a_instrução_0f ,
       \instrucao_01_1_é_a_instrução_01 , \instrucao_02_1_é_a_instrução_02 ,
       \instrucao_03_1_é_a_instrução_03 , \instrucao_07_1_é_a_instrução_07 ,
       \instrucao_08_1_é_a_instrução_08 , \instrucao_09_1_é_a_instrução_09 , not_1_out, not_2_out, not_3_out,
       or_1_out, \se_instrução____0f_e__AC____0_out , ula_16bits_1_o1;
  wire [7:0] controlled_buffer_1_out, PC_q, \posição_atual_q , ula_somador8bits_1_a___b;
  wire [15:0] AC_q, controlled_buffer_3_out, controlled_buffer_4_out, IR_q, ram_1_data, ula_16bits_1_r;

  and and_1 (and_1_out, \instrucao_0f_1_é_a_instrução_0f , ~ula_16bits_1_o1);  // AND_Gate
  and \se_instrução____0f_e__AC____0  (\se_instrução____0f_e__AC____0_out , \instrucao_0f_1_é_a_instrução_0f , ula_16bits_1_o1);
  Clock clock_1 (.out(clock_1_out));
  and and_2 (and_2_out, eu_sei_que_vai_ser_sempre_1__mas_fica_mais_intuitivo_out, ~and_1_out, not_2_out);  // AND_Gate
  assign controlled_buffer_1_out = and_2_out ? IR_q[7:0] : 8'bz;  // Controlled_Buffer controlled_buffer_1
  assign controlled_buffer_1_out = or_1_out ? ula_somador8bits_1_a___b : 8'bz;  // Controlled_Buffer controlled_buffer_2
  or or_1 (or_1_out, and_3_out, and_1_out);
  and and_3 (and_3_out, clock_1_out, \clock_com_meia_frequência_qn );
  or eu_sei_que_vai_ser_sempre_1__mas_fica_mais_intuitivo (eu_sei_que_vai_ser_sempre_1__mas_fica_mais_intuitivo_out, and_1_out, \se_instrução____0f_e__AC____0_out , \instrucao_08_1_é_a_instrução_08 , \instrucao_0a_1_é_a_instrução_0a , \instrucao_07_1_é_a_instrução_07 , \instrucao_03_1_é_a_instrução_03 , \instrucao_02_1_é_a_instrução_02 , \instrucao_01_1_é_a_instrução_01 );
  not not_1 (not_1_out, eu_sei_que_vai_ser_sempre_1__mas_fica_mais_intuitivo_out);
  not not_2 (not_2_out, and_3_out);
  ULA_somador8bits ula_somador8bits_1 (
    .A(8'h1), .B(\posição_atual_q ), .A___B(ula_somador8bits_1_a___b), .cin(1'b0));  // open: cout, coutanterior
  Counter #(.trigger("falling")) PC (
    .load(eu_sei_que_vai_ser_sempre_1__mas_fica_mais_intuitivo_out), .D(controlled_buffer_1_out),
    .count(not_1_out), .Q(PC_q), .clk(clock_1_out), .clr(\instrucao_09_1_é_a_instrução_09 ));  // open: carry
  J_K_Flip_Flop \clock_com_meia_frequência  (
    .J(clock_1_out), .clk(clock_1_out), .K(clock_1_out), .Q(\clock_com_meia_frequência_q ),
    .Qn(\clock_com_meia_frequência_qn ));  // open: preset, en, reset
  Register \posição_atual  (.D(PC_q), .Q(\posição_atual_q ), .clk(\clock_com_meia_frequência_q ));  // open: en, clr
  RAM #(.dataWidth(16)) ram_1 (.addr(PC_q), .data(ram_1_data), .clk(clock_1_out), .ld(not_3_out));  // open: sel, clr
  assign controlled_buffer_3_out = \instrucao_01_1_é_a_instrução_01  ? ram_1_data : 16'bz;  // Controlled_Buffer controlled_buffer_3
  Register #(.width(16), .trigger("falling")) AC (
    .D(controlled_buffer_3_out), .Q(AC_q), .clk(\clock_com_meia_frequência_q ));  // open: en, clr
  assign controlled_buffer_4_out = \instrucao_03_1_é_a_instrução_03  ? ram_1_data : 16'bz;  // Controlled_Buffer controlled_buffer_4
  assign controlled_buffer_3_out = \instrucao_03_1_é_a_instrução_03  ? ula_16bits_1_r : 16'bz;  // Controlled_Buffer controlled_buffer_5
  assign ram_1_data = and_6_out ? AC_q : 16'bz;  // Controlled_Buffer controlled_buffer_6
  ULA_16Bits ula_16bits_1 (
    .S(1'b0), .A(controlled_buffer_4_out), .B(AC_q), .R(ula_16bits_1_r), .O1(ula_16bits_1_o1));  // open: O0, O2, O3
  assign controlled_buffer_4_out = \instrucao_0f_1_é_a_instrução_0f  ? {16{1'b0}} : 16'bz;  // Controlled_Buffer controlled_buffer_7
  assign ram_1_data = and_7_out ? INPUT : 16'bz;  // Controlled_Buffer controlled_buffer_8
  assign OUTPUT = and_5_out ? ram_1_data : 16'bz;  // Controlled_Buffer controlled_buffer_9
  D_Flip_Flop d_ff_1 (
    .clk(clock_1_out), .D(\instrucao_08_1_é_a_instrução_08 ), .Q(d_ff_1_q));  // open: Qn, preset, en, reset
  and and_4 (and_4_out, d_ff_1_q, \instrucao_08_1_é_a_instrução_08 );
  D_Flip_Flop #(.trigger("falling")) d_ff_2 (
    .clk(clock_1_out), .D(and_4_out), .Qn(d_ff_2_qn));  // open: Q, preset, en, reset
  and and_5 (and_5_out, and_4_out, d_ff_2_qn);
  Register #(.width(16)) IR (
    .D(ram_1_data), .Q(IR_q), .clk(\clock_com_meia_frequência_q ), .clr(\instrucao_09_1_é_a_instrução_09 ));  // open: en
  not not_3 (not_3_out, \Escreverá_do_endereço_out );
  Instrucao_01 instrucao_01_1 (.\instrução (IR_q[15:8]), .\É_a_instrução_01 (\instrucao_01_1_é_a_instrução_01 ));
  Instrucao_02 instrucao_02_1 (.\instrução (IR_q[15:8]), .\É_a_instrução_02 (\instrucao_02_1_é_a_instrução_02 ));
  Instrucao_03 instrucao_03_1 (.\instrução (IR_q[15:8]), .\É_a_instrução_03 (\instrucao_03_1_é_a_instrução_03 ));
  Instrucao_07 instrucao_07_1 (.\instrução (IR_q[15:8]), .\É_a_instrução_07 (\instrucao_07_1_é_a_instrução_07 ));
  Instrucao_08 instrucao_08_1 (.\instrução (IR_q[15:8]), .\É_a_instrução_08 (\instrucao_08_1_é_a_instrução_08 ));
  Instrucao_09 instrucao_09_1 (.\instrução (IR_q[15:8]), .\É_a_instrução_09 (\instrucao_09_1_é_a_instrução_09 ));
  Instrucao_0a instrucao_0a_1 (.\instrução (IR_q[15:8]), .\É_a_instrução_0a (\instrucao_0a_1_é_a_instrução_0a ));
  Instrucao_0f instrucao_0f_1 (.\instrução (IR_q[15:8]), .\É_a_instrução_0f (\instrucao_0f_1_é_a_instrução_0f ));
  D_Flip_Flop d_ff_3 (
    .clk(clock_1_out), .D(\instrucao_02_1_é_a_instrução_02 ), .Qn(d_ff_3_qn));  // open: Q, preset, en, reset
  D_Flip_Flop d_ff_4 (
    .clk(clock_1_out), .D(\instrucao_07_1_é_a_instrução_07 ), .Qn(d_ff_4_qn));  // open: Q, preset, en, reset
  and and_6 (and_6_out, \instrucao_02_1_é_a_instrução_02 , d_ff_3_qn);
  and and_7 (and_7_out, \instrucao_07_1_é_a_instrução_07 , d_ff_4_qn);
  or \Escreverá_do_endereço  (\Escreverá_do_endereço_out , and_7_out, and_6_out);

  // Notes on the sheet:
  //   se for a instrução 0a, ele colocará o PC no endereço requisitado
  //   se for a instrução 08, ele permitirá a gravação da leitura em OUTPUT
  //   se for a instrução 07, ele colocará o PC no endereço requisitado e permitirá a gravação do valor lido
  //   se for a instrução 02, ele colocará o PC no endereço requisitado e permitirá a gravação do [AC] no endereço
  //   se for a instrução 01, ele colocará o PC no endereço requisitado e permitirá a gravação no AC
  //   se for a instrução 03, ele colocará o PC no endereço requisitado e permitirá a gravação no AC da soma em questão
  //   só imprimirá o segundo output
  //   endereço
  //   instrução
  //   Pare :D (vai congelar os registradores em 00)
  //   só vai escrever se forem as instruções 02 ou 07
  //   Os circuitos com flip-flops D são para que o circuito não realize uma ação duas vezes 
endmodule

module ULA_somador (
  input  cin,
  input  a,
  input  b,
  output cout,
  output \saída 
);

  wire and_1_out, and_2_out, xor_1_out;

  and and_1 (and_1_out, a, b);
  xor xor_1 (xor_1_out, b, a);
  and and_2 (and_2_out, cin, xor_1_out);
  xor xor_2 (\saída , xor_1_out, cin);
  or or_1 (cout, and_1_out, and_2_out);
endmodule

// Soma 1
module ULA_somador8bits (
  input  [7:0] A,
  input  [7:0] B,
  input  cin,
  output cout,
  output coutanterior,
  output [7:0] A___B
);

  wire ula_somador_3_cout, ula_somador_4_cout, ula_somador_5_cout, ula_somador_6_cout, ula_somador_7_cout,
       ula_somador_8_cout;

  ULA_somador ula_somador_1 (.a(B[7]), .b(A[7]), .cin(coutanterior), .cout(cout), .\saída (A___B[7]));
  ULA_somador ula_somador_2 (.a(B[6]), .b(A[6]), .cin(ula_somador_3_cout), .cout(coutanterior), .\saída (A___B[6]));
  ULA_somador ula_somador_3 (
    .a(B[5]), .b(A[5]), .cin(ula_somador_4_cout), .cout(ula_somador_3_cout), .\saída (A___B[5]));
  ULA_somador ula_somador_4 (
    .a(B[4]), .b(A[4]), .cin(ula_somador_6_cout), .cout(ula_somador_4_cout), .\saída (A___B[4]));
  ULA_somador ula_somador_5 (
    .a(B[2]), .b(A[2]), .cin(ula_somador_7_cout), .cout(ula_somador_5_cout), .\saída (A___B[2]));
  ULA_somador ula_somador_6 (
    .a(B[3]), .b(A[3]), .cin(ula_somador_5_cout), .cout(ula_somador_6_cout), .\saída (A___B[3]));
  ULA_somador ula_somador_7 (
    .a(B[1]), .b(A[1]), .cin(ula_somador_8_cout), .cout(ula_somador_7_cout), .\saída (A___B[1]));
  ULA_somador ula_somador_8 (.a(B[0]), .b(A[0]), .cin(cin), .cout(ula_somador_8_cout), .\saída (A___B[0]));

  // Notes on the sheet:
  //   Somando bit a bit e passando o bit 'que sobe' para a próxima soma
endmodule

module ULA_conversor (
  input  [7:0] A,
  output _128,
  output [7:0] minus_A
);

  wire ula_somador8bits_1_cout, ula_somador8bits_1_coutanterior;
  wire [7:0] not_1_out;

  assign not_1_out = ~A;  // NOT_Gate not_1, 8 bits wide
  ULA_somador8bits ula_somador8bits_1 (
    .cout(ula_somador8bits_1_cout), .coutanterior(ula_somador8bits_1_coutanterior), .A(not_1_out),
    .B({8{1'b0}}), .A___B(minus_A), .cin(1'b1));
  xor xor_1 (_128, ula_somador8bits_1_coutanterior, ula_somador8bits_1_cout);
endmodule

module ULA_comparador (
  input  A,
  input  B,
  output A___B,
  output A___B_2,
  output B___A
);

  wire and_2_out, and_3_out, not_1_out, not_2_out, not_3_out, not_4_out;

  not not_1 (not_1_out, A);
  not not_2 (not_2_out, B);
  not not_3 (not_3_out, A);
  not not_4 (not_4_out, B);
  and and_1 (A___B, not_1_out, B);
  and and_2 (and_2_out, not_2_out, not_3_out);
  and and_3 (and_3_out, B, A);
  and and_4 (B___A, not_4_out, A);
  or or_1 (A___B_2, and_2_out, and_3_out);
endmodule

module ULA_comparador8bits (
  input  [7:0] A,
  input  [7:0] B,
  output A___B,
  output A___B_2,
  output B___A
);

  wire and_1_out, and_2_out, and_4_out, and_6_out, and_7_out, and_8_out, and_9_out, not_1_out, not_2_out,
       or_1_out, ula_comparador_1_a___b_2, ula_comparador_1_b___a, ula_comparador_2_a___b_2,
       ula_comparador_2_b___a, ula_comparador_3_a___b_2, ula_comparador_3_b___a, ula_comparador_4_a___b_2,
       ula_comparador_4_b___a, ula_comparador_5_a___b_2, ula_comparador_5_b___a, ula_comparador_6_a___b_2,
       ula_comparador_6_b___a, ula_comparador_7_a___b_2, ula_comparador_7_b___a, ula_comparador_8_a___b,
       ula_comparador_8_a___b_2;

  ULA_comparador ula_comparador_1 (
    .A(A[0]), .B(B[0]), .A___B_2(ula_comparador_1_a___b_2), .B___A(ula_comparador_1_b___a));  // open: A___B
  ULA_comparador ula_comparador_2 (
    .A(A[1]), .B(B[1]), .A___B_2(ula_comparador_2_a___b_2), .B___A(ula_comparador_2_b___a));  // open: A___B
  ULA_comparador ula_comparador_3 (
    .A(A[2]), .B(B[2]), .A___B_2(ula_comparador_3_a___b_2), .B___A(ula_comparador_3_b___a));  // open: A___B
  ULA_comparador ula_comparador_4 (
    .A(A[3]), .B(B[3]), .A___B_2(ula_comparador_4_a___b_2), .B___A(ula_comparador_4_b___a));  // open: A___B
  ULA_comparador ula_comparador_5 (
    .A(A[4]), .B(B[4]), .A___B_2(ula_comparador_5_a___b_2), .B___A(ula_comparador_5_b___a));  // open: A___B
  ULA_comparador ula_comparador_6 (
    .A(A[5]), .B(B[5]), .A___B_2(ula_comparador_6_a___b_2), .B___A(ula_comparador_6_b___a));  // open: A___B
  ULA_comparador ula_comparador_7 (
    .A(A[6]), .B(B[6]), .A___B_2(ula_comparador_7_a___b_2), .B___A(ula_comparador_7_b___a));  // open: A___B
  ULA_comparador ula_comparador_8 (
    .A(A[7]), .B(B[7]), .A___B(ula_comparador_8_a___b), .A___B_2(ula_comparador_8_a___b_2));  // open: B___A
  and and_1 (and_1_out, ula_comparador_8_a___b_2, ula_comparador_7_b___a);
  or or_1 (or_1_out, ula_comparador_8_a___b, and_1_out, and_2_out, and_4_out, and_7_out, and_6_out, and_8_out, and_9_out);
  and and_2 (and_2_out, ula_comparador_8_a___b_2, ula_comparador_7_a___b_2, ula_comparador_6_b___a);
  and and_3 (A___B, or_1_out, not_2_out);
  and and_4 (and_4_out, ula_comparador_8_a___b_2, ula_comparador_7_a___b_2, ula_comparador_6_a___b_2, ula_comparador_5_b___a);
  not not_1 (not_1_out, or_1_out);
  and and_5 (B___A, not_1_out, not_2_out);
  and and_6 (and_6_out, ula_comparador_8_a___b_2, ula_comparador_7_a___b_2, ula_comparador_6_a___b_2, ula_comparador_5_a___b_2, ula_comparador_4_a___b_2, ula_comparador_3_b___a);
  and and_7 (and_7_out, ula_comparador_8_a___b_2, ula_comparador_7_a___b_2, ula_comparador_6_a___b_2, ula_comparador_5_a___b_2, ula_comparador_4_b___a);
  and and_8 (and_8_out, ula_comparador_8_a___b_2, ula_comparador_7_a___b_2, ula_comparador_6_a___b_2, ula_comparador_5_a___b_2, ula_comparador_4_a___b_2, ula_comparador_3_a___b_2, ula_comparador_2_b___a);
  not not_2 (not_2_out, A___B_2);
  and and_9 (and_9_out, ula_comparador_8_a___b_2, ula_comparador_7_a___b_2, ula_comparador_6_a___b_2, ula_comparador_5_a___b_2, ula_comparador_4_a___b_2, ula_comparador_3_a___b_2, ula_comparador_2_a___b_2, ula_comparador_1_b___a);
  and and_10 (A___B_2, ula_comparador_8_a___b_2, ula_comparador_7_a___b_2, ula_comparador_6_a___b_2, ula_comparador_5_a___b_2, ula_comparador_4_a___b_2, ula_comparador_3_a___b_2, ula_comparador_2_a___b_2, ula_comparador_1_a___b_2);
endmodule

// ULA
module ULA_main (
  input  [7:0] A,
  input  [7:0] B,
  input  S,
  output O0,
  output O1,
  output O2,
  output O3,
  output [7:0] A___B
);

  wire _128_____128_out, _128_out, and_1_out, and_2_out, and_4_out, not_1_out, ula_comparador8bits_1_a___b,
       ula_comparador8bits_1_a___b_2, ula_comparador8bits_1_b___a, ula_conversor_1__128,
       ula_somador8bits_1_cout, ula_somador8bits_1_coutanterior, xor_1_out;
  wire [7:0] multiplexer_1_out, ula_conversor_1_minus_a;

  xor xor_1 (xor_1_out, ula_somador8bits_1_cout, ula_somador8bits_1_coutanterior);
  ULA_comparador8bits ula_comparador8bits_1 (
    .A(A), .B(B), .A___B(ula_comparador8bits_1_a___b), .A___B_2(ula_comparador8bits_1_a___b_2),
    .B___A(ula_comparador8bits_1_b___a));
  ULA_somador8bits ula_somador8bits_1 (
    .cout(ula_somador8bits_1_cout), .coutanterior(ula_somador8bits_1_coutanterior), .A(A),
    .B(multiplexer_1_out), .A___B(A___B), .cin(1'b0));
  ULA_conversor ula_conversor_1 (.A(B), .minus_A(ula_conversor_1_minus_a), ._128(ula_conversor_1__128));
  Multiplexer #(.width(8), .disabled(0)) multiplexer_1 (
    .in0(B), .in1(ula_conversor_1_minus_a), .out(multiplexer_1_out), .sel(S));  // open: en
  not not_1 (not_1_out, xor_1_out);
  and _128 (_128_out, ula_conversor_1__128, S);
  and and_1 (and_1_out, not_1_out, ula_comparador8bits_1_a___b);
  and and_2 (and_2_out, not_1_out, ula_comparador8bits_1_a___b_2);
  and and_3 (O3, not_1_out, ula_comparador8bits_1_b___a);
  and _128_____128 (_128_____128_out, ula_comparador8bits_1_a___b_2, _128_out);
  and and_4 (and_4_out, _128_out, A[7]);
  and and_5 (O0, xor_1_out, ~_128_____128_out, ~and_4_out);  // AND_Gate
  or or_1 (O1, and_1_out, and_4_out);
  or or_2 (O2, and_2_out, _128_____128_out);
endmodule

// ULA
module ULA_16Bits (
  input  [15:0] A,
  input  [15:0] B,
  input  S,
  output O0,
  output O1,
  output O2,
  output O3,
  output [15:0] R
);

  wire [7:0] ula_main_1_a___b;

  ULA_main ula_main_1 (.S(S), .A(A[7:0]), .B(B[7:0]), .A___B(ula_main_1_a___b), .O0(O0), .O1(O1), .O2(O2), .O3(O3));
  assign R = {{8{1'b0}}, ula_main_1_a___b};  // Bit_Extender bit_extender_1

  // Notes on the sheet:
  //   Feita a alternativa B do enunciado (tratar apenas os 8 bits menos significativos)
endmodule

// 01 ?
module Instrucao_01 (
  input  [7:0] \instrução ,
  output \É_a_instrução_01 
);

  wire [7:0] not_1_out;

  assign not_1_out = ~\instrução ;  // NOT_Gate not_1, 8 bits wide
  and and_1 (\É_a_instrução_01 , ~not_1_out[0], not_1_out[1], not_1_out[2], not_1_out[3], not_1_out[4], not_1_out[5], not_1_out[6], not_1_out[7]);  // AND_Gate
endmodule

// 02 ?
module Instrucao_02 (
  input  [7:0] \instrução ,
  output \É_a_instrução_02 
);

  wire [7:0] not_1_out;

  assign not_1_out = ~\instrução ;  // NOT_Gate not_1, 8 bits wide
  and and_1 (\É_a_instrução_02 , not_1_out[0], ~not_1_out[1], not_1_out[2], not_1_out[3], not_1_out[4], not_1_out[5], not_1_out[6], not_1_out[7]);  // AND_Gate
endmodule

// 03 ?
module Instrucao_03 (
  input  [7:0] \instrução ,
  output \É_a_instrução_03 
);

  wire [7:0] not_1_out;

  assign not_1_out = ~\instrução ;  // NOT_Gate not_1, 8 bits wide
  and and_1 (\É_a_instrução_03 , ~not_1_out[0], ~not_1_out[1], not_1_out[2], not_1_out[3], not_1_out[4], not_1_out[5], not_1_out[6], not_1_out[7]);  // AND_Gate
endmodule

// 07 ?
module Instrucao_07 (
  input  [7:0] \instrução ,
  output \É_a_instrução_07 
);

  wire [7:0] not_1_out;

  assign not_1_out = ~\instrução ;  // NOT_Gate not_1, 8 bits wide
  and and_1 (\É_a_instrução_07 , ~not_1_out[0], ~not_1_out[1], ~not_1_out[2], not_1_out[3], not_1_out[4], not_1_out[5], not_1_out[6], not_1_out[7]);  // AND_Gate
endmodule

// 08 ?
module Instrucao_08 (
  input  [7:0] \instrução ,
  output \É_a_instrução_08 
);

  wire [7:0] not_1_out;

  assign not_1_out = ~\instrução ;  // NOT_Gate not_1, 8 bits wide
  and and_1 (\É_a_instrução_08 , not_1_out[0], not_1_out[1], not_1_out[2], ~not_1_out[3], not_1_out[4], not_1_out[5], not_1_out[6], not_1_out[7]);  // AND_Gate
endmodule

// 09 ?
module Instrucao_09 (
  input  [7:0] \instrução ,
  output \É_a_instrução_09 
);

  wire [7:0] not_1_out;

  assign not_1_out = ~\instrução ;  // NOT_Gate not_1, 8 bits wide
  and and_1 (\É_a_instrução_09 , ~not_1_out[0], not_1_out[1], not_1_out[2], ~not_1_out[3], not_1_out[4], not_1_out[5], not_1_out[6], not_1_out[7]);  // AND_Gate
endmodule

// 0a ?
module Instrucao_0a (
  input  [7:0] \instrução ,
  output \É_a_instrução_0a 
);

  wire [7:0] not_1_out;

  assign not_1_out = ~\instrução ;  // NOT_Gate not_1, 8 bits wide
  and and_1 (\É_a_instrução_0a , not_1_out[0], ~not_1_out[1], not_1_out[2], ~not_1_out[3], not_1_out[4], not_1_out[5], not_1_out[6], not_1_out[7]);  // AND_Gate
endmodule

// 0f ?
module Instrucao_0f (
  input  [7:0] \instrução ,
  output \É_a_instrução_0f 
);

  wire [7:0] not_1_out;

  assign not_1_out = ~\instrução ;  // NOT_Gate not_1, 8 bits wide
  and and_1 (\É_a_instrução_0f , ~not_1_out[0], ~not_1_out[1], ~not_1_out[2], ~not_1_out[3], not_1_out[4], not_1_out[5], not_1_out[6], not_1_out[7]);  // AND_Gate
endmodule
