// Logisim project ULA.circ as structural Verilog: 6 circuits, main circuit Somador
module Somador (
  input  cin,
  input  a,
  input  b,
  output cout,
  output \saída 
);

  wire and_1_out, and_2_out, xor_1_out;

  and and_1 (and_1_out, a, b);
  xor xor_1 (xor_1_out, b, a);
  and and_2 (and_2_out, cin, xor_1_out);
  xor xor_2 (\saída , xor_1_out, cin);
  or or_1 (cout, and_1_out, and_2_out);
endmodule

module Somador_8bits (
  input  [7:0] A,
  input  [7:0] B,
  input  cin,
  output cout,
  output coutanterior,
  output [7:0] A___B
);

  wire somador_3_cout, somador_4_cout, somador_5_cout, somador_6_cout, somador_7_cout, somador_8_cout;

  Somador somador_1 (.a(B[7]), .b(A[7]), .cin(coutanterior), .cout(cout), .\saída (A___B[7]));
  Somador somador_2 (.a(B[6]), .b(A[6]), .cin(somador_3_cout), .cout(coutanterior), .\saída (A___B[6]));
  Somador somador_3 (.a(B[5]), .b(A[5]), .cin(somador_4_cout), .cout(somador_3_cout), .\saída (A___B[5]));
  Somador somador_4 (.a(B[4]), .b(A[4]), .cin(somador_6_cout), .cout(somador_4_cout), .\saída (A___B[4]));
  Somador somador_5 (.a(B[2]), .b(A[2]), .cin(somador_7_cout), .cout(somador_5_cout), .\saída (A___B[2]));
  Somador somador_6 (.a(B[3]), .b(A[3]), .cin(somador_5_cout), .cout(somador_6_cout), .\saída (A___B[3]));
  Somador somador_7 (.a(B[1]), .b(A[1]), .cin(somador_8_cout), .cout(somador_7_cout), .\saída (A___B[1]));
  Somador somador_8 (.a(B[0]), .b(A[0]), .cin(cin), .cout(somador_8_cout), .\saída (A___B[0]));

  // Notes on the sheet:
  //   Somando bit a bit e passando o bit 'que sobe' para a próxima soma
endmodule

// - B
module Conversor_positivo_negativo (
  input  [7:0] A,
  output _128,
  output [7:0] minus_A
);

  wire somador_8bits_1_cout, somador_8bits_1_coutanterior;
  wire [7:0] not_1_out;

  assign not_1_out = ~A;  // NOT_Gate not_1, 8 bits wide
  Somador_8bits somador_8bits_1 (
    .cout(somador_8bits_1_cout), .coutanterior(somador_8bits_1_coutanterior), .A(not_1_out), .B({8{1'b0}}),
    .A___B(minus_A), .cin(1'b1));
  xor xor_1 (_128, somador_8bits_1_coutanterior, somador_8bits_1_cout);
endmodule

module main (
  input  [7:0] A,
  input  [7:0] B,
  input  S,
  output O0,
  output O1,
  output O2,
  output O3,
  output [7:0] A___B
);

  wire _128_____128_out, _128_out, and_1_out, and_2_out, and_4_out, comparador_8_bits_1_a___b,
       comparador_8_bits_1_a___b_2, comparador_8_bits_1_b___a, conversor_positivo_negativo_1__128, not_1_out,
       Somador_cout, Somador_coutanterior, xor_1_out;
  wire [7:0] conversor_positivo_negativo_1_minus_a, multiplexer_1_out;

  xor xor_1 (xor_1_out, Somador_cout, Somador_coutanterior);
  Comparador_8_bits comparador_8_bits_1 (
    .A(A), .B(B), .A___B(comparador_8_bits_1_a___b), .A___B_2(comparador_8_bits_1_a___b_2),
    .B___A(comparador_8_bits_1_b___a));
  Somador_8bits Somador (
    .cout(Somador_cout), .coutanterior(Somador_coutanterior), .A(A), .B(multiplexer_1_out), .A___B(A___B),
    .cin(1'b0));
  Conversor_positivo_negativo conversor_positivo_negativo_1 (
    .A(B), .minus_A(conversor_positivo_negativo_1_minus_a), ._128(conversor_positivo_negativo_1__128));
  Multiplexer #(.width(8), .disabled(0)) multiplexer_1 (
    .in0(B), .in1(conversor_positivo_negativo_1_minus_a), .out(multiplexer_1_out), .sel(S));  // open: en
  not not_1 (not_1_out, xor_1_out);
  and _128 (_128_out, conversor_positivo_negativo_1__128, S);
  and and_1 (and_1_out, not_1_out, comparador_8_bits_1_a___b);
  and and_2 (and_2_out, not_1_out, comparador_8_bits_1_a___b_2);
  and and_3 (O3, not_1_out, comparador_8_bits_1_b___a);
  and _128_____128 (_128_____128_out, comparador_8_bits_1_a___b_2, _128_out);
  and and_4 (and_4_out, _128_out, A[7]);
  and and_5 (O0, xor_1_out, ~_128_____128_out, ~and_4_out);  // AND_Gate
  or or_1 (O1, and_1_out, and_4_out);
  or or_2 (O2, and_2_out, _128_____128_out);
endmodule

module Comparador (
  input  A,
  input  B,
  output A___B,
  output A___B_2,
  output B___A
);

  wire and_2_out, and_3_out, not_1_out, not_2_out, not_3_out, not_4_out;

  not not_1 (not_1_out, A);
  not not_2 (not_2_out, B);
  not not_3 (not_3_out, A);
  not not_4 (not_4_out, B);
  and and_1 (A___B, not_1_out, B);
  and and_2 (and_2_out, not_2_out, not_3_out);
  and and_3 (and_3_out, B, A);
  and and_4 (B___A, not_4_out, A);
  or or_1 (A___B_2, and_2_out, and_3_out);
endmodule

module Comparador_8_bits (
  input  [7:0] B,
  input  [7:0] A,
  output A___B,
  output A___B_2,
  output B___A
);

  wire and_1_out, and_2_out, and_4_out, and_6_out, and_7_out, and_8_out, and_9_out, comparador_1_a___b_2,
       comparador_1_b___a, comparador_2_a___b_2, comparador_2_b___a, comparador_3_a___b_2,
       comparador_3_b___a, comparador_4_a___b_2, comparador_4_b___a, comparador_5_a___b_2,
       comparador_5_b___a, comparador_6_a___b_2, comparador_6_b___a, comparador_7_a___b_2,
       comparador_7_b___a, comparador_8_a___b, comparador_8_a___b_2, not_1_out, not_2_out, or_1_out;

  Comparador comparador_1 (
    .A(A[0]), .B(B[0]), .A___B_2(comparador_1_a___b_2), .B___A(comparador_1_b___a));  // open: A___B
  Comparador comparador_2 (
    .A(A[1]), .B(B[1]), .A___B_2(comparador_2_a___b_2), .B___A(comparador_2_b___a));  // open: A___B
  Comparador comparador_3 (
    .A(A[2]), .B(B[2]), .A___B_2(comparador_3_a___b_2), .B___A(comparador_3_b___a));  // open: A___B
  Comparador comparador_4 (
    .A(A[3]), .B(B[3]), .A___B_2(comparador_4_a___b_2), .B___A(comparador_4_b___a));  // open: A___B
  Comparador comparador_5 (
    .A(A[4]), .B(B[4]), .A___B_2(comparador_5_a___b_2), .B___A(comparador_5_b___a));  // open: A___B
  Comparador comparador_6 (
    .A(A[5]), .B(B[5]), .A___B_2(comparador_6_a___b_2), .B___A(comparador_6_b___a));  // open: A___B
  Comparador comparador_7 (
    .A(A[6]), .B(B[6]), .A___B_2(comparador_7_a___b_2), .B___A(comparador_7_b___a));  // open: A___B
  Comparador comparador_8 (
    .A(A[7]), .B(B[7]), .A___B(comparador_8_a___b), .A___B_2(comparador_8_a___b_2));  // open: B___A
  and and_1 (and_1_out, comparador_8_a___b_2, comparador_7_b___a);
  or or_1 (or_1_out, comparador_8_a___b, and_1_out, and_2_out, and_4_out, and_6_out, and_7_out, and_8_out, and_9_out);
  and and_2 (and_2_out, comparador_8_a___b_2, comparador_7_a___b_2, comparador_6_b___a);
  and and_3 (A___B, or_1_out, not_2_out);
  and and_4 (and_4_out, comparador_8_a___b_2, comparador_7_a___b_2, comparador_6_a___b_2, comparador_5_b___a);
  not not_1 (not_1_out, or_1_out);
  and and_5 (B___A, not_1_out, not_2_out);
  and and_6 (and_6_out, comparador_8_a___b_2, comparador_7_a___b_2, comparador_6_a___b_2, comparador_5_a___b_2, comparador_4_b___a);
  and and_7 (and_7_out, comparador_8_a___b_2, comparador_7_a___b_2, comparador_6_a___b_2, comparador_5_a___b_2, comparador_4_a___b_2, comparador_3_b___a);
  and and_8 (and_8_out, comparador_8_a___b_2, comparador_7_a___b_2, comparador_6_a___b_2, comparador_5_a___b_2, comparador_4_a___b_2, comparador_3_a___b_2, comparador_2_b___a);
  not not_2 (not_2_out, A___B_2);
  and and_9 (and_9_out, comparador_8_a___b_2, comparador_7_a___b_2, comparador_6_a___b_2, comparador_5_a___b_2, comparador_4_a___b_2, comparador_3_a___b_2, comparador_2_a___b_2, comparador_1_b___a);
  and and_10 (A___B_2, comparador_8_a___b_2, comparador_7_a___b_2, comparador_6_a___b_2, comparador_5_a___b_2, comparador_4_a___b_2, comparador_3_a___b_2, comparador_2_a___b_2, comparador_1_a___b_2);
endmodule
