// Logisim project ep3bool.circ as structural Verilog
module main (
  input  [15:0] in_1,
  input  contador___0_input___1,
  input  inic___1,
  input  caminhos,
  input  reset___1,
  input  write___0_read___1,
  output [15:0] out_7,
  output [15:0] out_8
);

  wire clock_out, not_1_out;
  wire [7:0] counter_1_q;
  wire [15:0] bit_extender_1_out, multiplexer_1_out, ram_1_data;

  Clock clock (.out(clock_out));
  Counter counter_1 (.count(inic___1), .Q(counter_1_q), .clk(clock_out), .clr(reset___1));  // open: load, D, carry
  assign bit_extender_1_out = {{8{1'b0}}, counter_1_q};  // Bit_Extender bit_extender_1
  RAM #(.dataWidth(16)) ram_1 (
    .addr(counter_1_q), .data(ram_1_data), .clk(clock_out), .ld(write___0_read___1));  // open: sel, clr
  not not_1 (not_1_out, write___0_read___1);
  Multiplexer #(.width(16)) multiplexer_1 (
    .in0(bit_extender_1_out), .in1(in_1), .out(multiplexer_1_out), .sel(contador___0_input___1));  // open: en
  assign ram_1_data = not_1_out ? multiplexer_1_out : 16'bz;  // Controlled_Buffer controlled_buffer_1
  Demultiplexer #(.width(16)) demultiplexer_1 (
    .out0(out_7), .out1(out_8), .in(ram_1_data), .sel(caminhos));  // open: en
endmodule
