// Logisim project somador.circ as structural Verilog: 2 circuits, main circuit Somador
module Somador (
  input  cin,
  input  a,
  input  b,
  output cout,
  output \saída 
);

  wire and_1_out, and_2_out, xor_1_out;

  and and_1 (and_1_out, a, b);
  xor xor_1 (xor_1_out, b, a);
  and and_2 (and_2_out, cin, xor_1_out);
  xor xor_2 (\saída , xor_1_out, cin);
  or or_1 (cout, and_1_out, and_2_out);
endmodule

module Somador_4_bits (
  input  a0,
  input  a1,
  input  a2,
  input  a3,
  input  b3,
  input  b2,
  input  b1,
  input  b0,
  input  cin,
  output cout,
  output s3,
  output s2,
  output s1,
  output s0
);

  wire somador_2_cout, somador_3_cout, somador_4_cout;

  Somador somador_1 (.a(b3), .b(a0), .cin(somador_2_cout), .cout(cout), .\saída (s3));
  Somador somador_2 (.a(b2), .b(a1), .cin(somador_3_cout), .cout(somador_2_cout), .\saída (s2));
  Somador somador_3 (.a(b1), .b(a2), .cin(somador_4_cout), .cout(somador_3_cout), .\saída (s1));
  Somador somador_4 (.a(b0), .b(a3), .cin(cin), .cout(somador_4_cout), .\saída (s0));
endmodule
